# Fritzing sketch LED오디오 설계도 (saved by Fritzing 0.9.6b)
breadboards: 2

parts:
  LED1 = LED - 5mm [color="Red (633nm)" current=0.030 package="5 mm [THT]"]
  LED2 = LED - 5mm [color="Yellow (595nm)" current=0.030 package="5 mm [THT]"]
  LED3 = LED - 5mm [color="Green (570nm)" current=0.030 package="5 mm [THT]"]
  LED4 = LED - 5mm [color="Blue (525nm)" current=0.030 package="5 mm [THT]"]
  LED5 = LED - 5mm [color="White (4500K)" current=0.030 package="5 mm [THT]"]
  LED6 = LED - 5mm [color="Red (633nm)" current=0.030 package="5 mm [THT]"]
  LED7 = LED - 5mm [color="Yellow (595nm)" current=0.030 package="5 mm [THT]"]
  LED8 = LED - 5mm [color="Green (570nm)" current=0.030 package="5 mm [THT]"]
  LED9 = LED - 5mm [color="Blue (525nm)" current=0.030 package="5 mm [THT]"]
  LED10 = LED - 5mm [color="White (4500K)" current=0.030 package="5 mm [THT]"]
  R1 = Resistor [tolerance=±5% power=0.25 resistance=220 package=THT]
  부품1 = Arduino Uno (Rev3)
  J1 = Piezo Speaker

nets:
  N1: LED1.cathode, 부품1.D2
  N2: LED1.anode, LED2.anode, LED3.anode, LED4.anode, LED5.anode, LED6.anode, LED7.anode, LED8.anode, LED9.anode, LED10.anode, R1.Pin_0, R1.Pin_1, 부품1.GND, J1.pin1
  N3: LED2.cathode, 부품1.D3_PWM
  N4: LED3.cathode, 부품1.D4
  N5: LED4.cathode, 부품1.D5_PWM
  N6: LED5.cathode, 부품1.D6_PWM
  N7: LED6.cathode, 부품1.D7
  N8: LED7.cathode, 부품1.D8
  N9: LED8.cathode, 부품1.D9_PWM
  N10: LED9.cathode, 부품1.D10_PWM/SS
  N11: LED10.cathode, 부품1.D12/MISO
  N12: 부품1.D13/SCK, J1.pin2
